# Fritzing sketch ATTinyDebugTools (saved by Fritzing 0.9.9b)
circuit board: 8.46667cm x 5.64444cm
breadboards: 1

parts:
  Part1 = Arduino Uno (Rev3)
  C1 = Electrolytic Capacitor [capacitance=2.2µF voltage=35V package="100 mil [THT, electrolytic]"]
  D1 = Rectifier Diode [part_number=1N4001 package="300 mil [THT]"]
  D3 = Rectifier Diode [part_number=1N4001 package="300 mil [THT]"]
  C2 = Electrolytic Capacitor [capacitance=0.22µF voltage=35V package="100 mil [THT, electrolytic]"]
  C3 = Electrolytic Capacitor [capacitance=0.22µF voltage=35V package="100 mil [THT, electrolytic]"]
  R9 = Resistor [tolerance=±5% resistance=1k power=0.25 package="0805 [SMD]"]
  U1 = attiny85 [package=dip]
  D4 = Rectifier Diode [part_number=1N4001 package="300 mil [THT]"]
  R8 = Resistor [tolerance=±5% resistance=100k power=0.25 package="0805 [SMD]"]
  U2 = SWITCH_SPDT [package=kps-1290]
  R4 = Resistor [tolerance=±5% resistance=1k package="0805 [SMD]"]
  R7 = Resistor [tolerance=±5% resistance=470k power=0.25 package="0805 [SMD]"]
  R6 = Resistor [tolerance=±5% resistance=10k power=0.25 package="0805 [SMD]"]
  C4 = Electrolytic Capacitor [capacitance=0.22µF voltage=35V package="100 mil [THT, electrolytic]"]
  D2 = Rectifier Diode [part_number=1N4001 package="300 mil [THT]"]
  R3 = Resistor [tolerance=±5% resistance=1k power=0.25 package=THT]
  R2 = Resistor [tolerance=±5% resistance=1k power=0.25 package=THT]
  R1 = Resistor [tolerance=±5% resistance=1k power=0.25 package=THT]
  U4 = SWITCH_SPDT [package=kps-1290]
  Q1 = NPN-Transistor [package="TO92 [THT]"]

nets:
  N1: Part1.A0, R8.Pin_0, R7.Pin_1
  N2: Part1.D8, U2.S
  N3: Part1.D9_PWM, R4.Pin_1
  N4: Part1.D10_PWM/SS, U1.Pin_8
  N5: Part1.D11_PWM/MOSI, R3.Pin_1
  N6: Part1.D12/MISO, R2.Pin_1
  N7: Part1.D13/SCK, R1.Pin_1
  N8: Part1.GND, C1.-, U1.Pin_4, R8.Pin_1, U2.P, Q1.E
  N9: Part1.D2, C2.+, C3.+
  N10: Part1.D3_PWM, C4.+
  N11: Part1.D4, D4.anode
  N12: Part1.D5_PWM, R6.Pin_1
  N13: Part1.D6_PWM, U4.O
  N14: C1.+, D1.cathode, R9.Pin_1, R7.Pin_0, Q1.B
  N15: D1.anode, C3.-, D2.cathode
  N16: D3.cathode, C4.-, D2.anode
  N17: D3.anode, C2.-, D4.cathode
  N18: R9.Pin_0, U4.S
  N19: U1.Pin_1, U4.P
  N20: U1.Pin_2, R4.Pin_0
  N21: U1.Pin_5, R3.Pin_0
  N22: U1.Pin_6, R2.Pin_0
  N23: U1.Pin_7, R1.Pin_0
  N24: R6.Pin_0, Q1.C
